# Fritzing sketch mPod_BreadBoard (saved by Fritzing 0.9.10b)
breadboards: 2

parts:
  Part1 = Adafruit ESP32 Feather V2
  Part2 = Adafruit VS1053 Codec + MicroSD Breakout - MP3/WAV/MIDI/OGG [part_number="Adafruit #1381"]
  Part3 = Adafruit ANO Rotary Navigation Encoder Breakout [part_number="Adafruit #5221"]
  Part4 = Adafruit 1.3in 240x240 IPS TFT [part_number="Adafruit #4313"]
  U1 = 2.5mm Audio Jack [package=stereojack2.5mm_stereojack2.5mm]

nets:
  N1: Part1.SDA, Part1.IO27, Part2.XDCS_5V, Part4.TFTCS
  N2: Part1.I37, Part3.SW2
  N3: Part1.IO8, Part2.SDCS_5V
  N4: Part1.RX, Part2.CS_5V
  N5: Part1.MISO, Part2.MISO
  N6: Part1.MOSI, Part2.MOSI_5V
  N7: Part1.SCK, Part2.SCLK_5V
  N8: Part1.A5, Part4.TFTDC
  N9: Part1.A4, Part3.SW3
  N10: Part1.A3, Part3.SW4
  N11: Part1.A2, Part3.SW5
  N12: Part1.A0, Part4.BACKLIGHT
  GND: Part1.GND, Part2.GND, Part4.GND
  VIN: Part1.3.3V, Part2.VIN, Part3.COMA, Part3.COMB, Part4.VIN
  N13: Part1.IO13, Part2.DREQ
  N14: Part1.IO12, Part4.MOSI
  N15: Part1.IO33, Part3.ENC_A
  N16: Part1.IO15, Part3.ENC_B
  N17: Part1.IO32, Part3.SW1
  N18: Part1.IO14, Part4.SCK
  N19: Part1.SCL, Part2.RST_5V
  N20: Part2.R_OUT, U1.RIGHT
  N21: Part2.L_OUT, U1.LEFT
  N22: Part2.AGND, U1.GROUND

custom parts:
  Adafruit VS1053 Codec + MicroSD Breakout - MP3/WAV/MIDI/OGG: This breakout board is the ultimate companion for the VLSI VS1053B DSP codec chip. The VS1053 can decode a wide variety of audio formats such as MP3, AAC, Ogg Vorbis, WMA, MIDI, FLAC, WAV (PCM and ADPCM). It can also be used to record audio in both PCM (WAV) and compressed Ogg Vorbis. You can do all sorts of stuff with the audio as well such as adjusting bass, treble, and volume digitally.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
  Adafruit ANO Rotary Navigation Encoder Breakout: The ANO rotary encoder wheel is a funky user interface element is reminiscent of the original clicking scroll wheel interface on the first iPods. It's a nifty kit, but the pin-out is a little odd, so we made a handy breakout board that converts the funky pin set into a straight forward, breadboard-friendly header strip. This is just the PCB for the ANO encoder, the encoder is NOT included!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
  Adafruit 1.3in 240x240 IPS TFT: We've been looking for a display like this for a long time - it's so small only 1.3" diagonal but has a high density 260 ppi, 240x240 pixel display with full-angle viewing. It looks a lot like our 1.44" 128x128 display, but has 4x as many pixels and looks great at any angle. We've seen displays of this caliber used in smartwatches and small electronic devices but they've always been MIPI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
  2.5mm Audio Jack: Simple 2.5mm common PCB mount audio jack. SKU: PRT-08032
